# Fritzing sketch 2164VCA_Test (saved by Fritzing 0.9.4)
breadboards: 1

parts:
  IC1 = IC, DIP package, 16 pins [chip_label=V2164]
  C1 = Ceramic Capacitor [capacitance=100nF package="100 mil [THT, multilayer]"]
  C2 = Ceramic Capacitor [capacitance=100nF package="100 mil [THT, multilayer]"]
  R2 = Resistor [tolerance=±5% resistance=560 package=THT]
  R3 = Resistor [tolerance=±5% resistance=27k package=THT]
  R4 = Resistor [tolerance=±5% resistance=6.8k package=THT]
  IC2 = Dual Op-Amp [package=dip08]
  C5 = Ceramic Capacitor [capacitance=100nF package="100 mil [THT, multilayer]"]
  C6 = Ceramic Capacitor [capacitance=100nF package="100 mil [THT, multilayer]"]
  R5 = Resistor [tolerance=±5% resistance=33k package=THT]
  C7 = Ceramic Capacitor [capacitance=100nF package="100 mil [THT, multilayer]"]
  C4 = Film/Foil Capacitor [capacitance=100nF voltage=35V package="5mm [THT, pp]"]
  C8 = Electrolytic Capacitor [capacitance=1µF package="100 mil [THT, electrolytic]"]
  C9 = Electrolytic Capacitor [capacitance=1µF package="100 mil [THT, electrolytic]"]
  IC3 = Dual Op-Amp [package=dip08]
  C10 = Ceramic Capacitor [capacitance=100nF package="100 mil [THT, multilayer]"]
  C11 = Ceramic Capacitor [capacitance=100nF package="100 mil [THT, multilayer]"]
  R6 = Resistor [tolerance=±5% resistance=33k package=THT]
  C12 = Ceramic Capacitor [capacitance=100nF package="100 mil [THT, multilayer]"]
  R7 = Resistor [tolerance=±5% resistance=100k package=THT]
  R8 = Rotary Potentiometer (Small) [maximum_resistance=100kΩ package=THT]
  R9 = TRIMPOT [package=trimpot_pth_s3_lock]
  R10 = Resistor [tolerance=±5% resistance=27k package=THT]
  R11 = Resistor [tolerance=±5% resistance=100k package=THT]
  Q1 = NPN-Transistor [package="TO92 [THT]"]
  R12 = Resistor [tolerance=±5% resistance=220 package=THT]
  LED1 = LED - 5mm [color="Red (633nm)" package="5 mm [THT]"]
  D1 = Rectifier Diode [part_number=1N4001 package="300 mil [THT]"]
  R13 = Rotary Potentiometer (Small) [maximum_resistance=100kΩ package=THT]

nets:
  N1: IC1.pin1, R4.Pin_1
  N2: IC1.pin2, R2.Pin_1, R3.Pin_1
  N3: IC1.pin3, IC3.A_OUT, R6.Pin_0, C12.0
  N4: IC1.pin4, IC2.A_-IN, R5.Pin_1, C7.1
  N5: IC1.pin6, IC1.pin7, IC1.pin8, IC1.pin10, IC1.pin11, IC1.pin14, IC1.pin15, C1.0, C2.1, IC2.A_+IN, IC2.B_+IN, C5.0, C6.0, C4.-, C8.-, C9.+, IC3.B_+IN, C10.0, C11.1, R8.leg1, R9.CCW, LED1.cathode, D1.anode, R13.leg1
  N6: IC1.pin9, C2.0, IC2.A_V-, C6.1, C9.-, IC3.A_V-, C11.0
  N7: IC1.pin16, C1.1, R4.Pin_0, IC2.A_V+, C5.1, C8.+, IC3.A_V+, C10.1, R10.Pin_0, R12.Pin_0
  N8: R2.Pin_0, C4.+
  N9: R3.Pin_0, R13.wiper
  N10: IC2.A_OUT, R5.Pin_0, C7.0
  N11: IC2.B_-IN, IC2.B_OUT
  N12: IC3.A_-IN, R6.Pin_1, C12.1, R7.Pin_0
  N13: IC3.A_+IN, R9.WIPER
  N14: IC3.B_-IN, IC3.B_OUT
  N15: R7.Pin_1, R8.wiper, R11.Pin_0
  N16: R9.CW, R10.Pin_1
  N17: R11.Pin_1, Q1.C, D1.cathode
  N18: Q1.E, LED1.anode
  N19: Q1.B, R12.Pin_1

notes:
  CV
  50k/B
  OUT
  GND
  +12V
  -12V
  GND
  V2164
  1 MODE 16 V+
  2 IIN1 15 IIN4
  3 VC1 14 VC4
  4 IOUT1 13 IOUT4
  5 IOUT2 12 IOUT3
  6 VC2 11 VC3
  7 IIN2 10 IIN3
  8 GND 9 V-
  IN
  100k/A
